// Digital circuit 4_Registros.dig as structural Verilog
module _4_Registros (
  input  Sel,
  input  Enable,
  input  Clock,
  input  Clear,
  input  D0,
  input  D1,
  input  D2,
  input  D3,
  output out_9,
  output out_10,
  output out_11,
  output out_12
);

  wire multiplexer_1_out, multiplexer_2_out, multiplexer_3_out, multiplexer_4_out;

  Multiplexer multiplexer_1 (.sel(Enable), .in_0(out_9), .in_1(D3), .out(multiplexer_1_out));
  D_FF_AS d_ff_as_1 (.Set(Sel), .D(multiplexer_1_out), .C(Clock), .Clr(Clear), .Q(out_9));  // open: nQ
  Multiplexer multiplexer_2 (.sel(Enable), .in_0(out_10), .in_1(D2), .out(multiplexer_2_out));
  D_FF_AS d_ff_as_2 (.Set(Sel), .D(multiplexer_2_out), .C(Clock), .Clr(Clear), .Q(out_10));  // open: nQ
  Multiplexer multiplexer_3 (.sel(Enable), .in_0(out_11), .in_1(D1), .out(multiplexer_3_out));
  D_FF_AS d_ff_as_3 (.Set(Sel), .D(multiplexer_3_out), .C(Enable), .Clr(Clear), .Q(out_11));  // open: nQ
  Multiplexer multiplexer_4 (.sel(Enable), .in_0(out_12), .in_1(D0), .out(multiplexer_4_out));
  D_FF_AS d_ff_as_4 (.Set(Sel), .D(multiplexer_4_out), .C(Clock), .Clr(Clear), .Q(out_12));  // open: nQ

  // Notes on the sheet:
  //   REGISTRO DE DIRECCIÓN
endmodule
